# Fritzing sketch TeenAstroHandV0 (saved by Fritzing 0.9.3b)
circuit board: 5.55cm x 9cm
breadboards: 1

parts:
  WeMos_D1_Mini1 = WeMos D1 Mini
  C3 = Ceramic Capacitor [capacitance=100nF package="200 mil [THT, multilayer]"]
  C1 = Ceramic Capacitor [capacitance=100nF package="200 mil [THT, multilayer]"]
  C7 = Ceramic Capacitor [capacitance=100nF package="200 mil [THT, multilayer]"]
  C4 = Ceramic Capacitor [capacitance=100nF package="200 mil [THT, multilayer]"]
  C6 = Ceramic Capacitor [capacitance=100nF package="200 mil [THT, multilayer]"]
  C5 = Ceramic Capacitor [capacitance=100nF package="200 mil [THT, multilayer]"]
  5V_GND_SCL_SDA = female pin header, 4 pins [form="♀ (female)"]
  5V_GND_RX_TX = female pin header, 4 pins [form="♀ (female)"]
  J1 = female pin header, 7 pins [form="♀ (female)"]
  C2 = Ceramic Capacitor [capacitance=100nF package="200 mil [THT, multilayer]"]
  A0_GND_3V3 = female pin header, 3 pins [form="♀ (female)"]
  R1 = Resistor [tolerance=±5% resistance=220 package=THT]
  R2 = Resistor [tolerance=±5% resistance=220 package=THT]
  R3 = Resistor [tolerance=±5% resistance=220 package=THT]
  R4 = Resistor [tolerance=±5% resistance=220 package=THT]
  R5 = Resistor [tolerance=±5% resistance=220 package=THT]
  R6 = Resistor [tolerance=±5% resistance=220 package=THT]
  R7 = Resistor [tolerance=±5% resistance=220 package=THT]
  GND_3V3 = female pin header, 2 pins [form="♀ (female)"]

nets:
  N1: WeMos_D1_Mini1.3V3, A0_GND_3V3.pin1, R6.Pin_0, R7.Pin_0, GND_3V3.pin1
  N2: WeMos_D1_Mini1.5V, 5V_GND_SCL_SDA.pin4, 5V_GND_RX_TX.pin4
  N3: WeMos_D1_Mini1.A0, A0_GND_3V3.pin3
  N4: WeMos_D1_Mini1.D0, C5.0, J1.pin3, R5.Pin_1
  N5: WeMos_D1_Mini1.D1, 5V_GND_SCL_SDA.pin2
  N6: WeMos_D1_Mini1.D2, 5V_GND_SCL_SDA.pin1
  N7: WeMos_D1_Mini1.D3, C6.0, J1.pin2, R6.Pin_1
  N8: WeMos_D1_Mini1.D4, C7.0, J1.pin1, R7.Pin_1
  N9: WeMos_D1_Mini1.D5, C4.0, J1.pin4, R4.Pin_1
  N10: WeMos_D1_Mini1.D6, C3.0, J1.pin5, R3.Pin_1
  N11: WeMos_D1_Mini1.D7, J1.pin6, C2.0, R2.Pin_1
  N12: WeMos_D1_Mini1.D8, C1.0, J1.pin7, R1.Pin_1
  GND: WeMos_D1_Mini1.G, C3.1, C1.1, C7.1, C4.1, C6.1, C5.1, 5V_GND_SCL_SDA.pin3, 5V_GND_RX_TX.pin3, C2.1, A0_GND_3V3.pin2, R1.Pin_0, R2.Pin_0, R3.Pin_0, R4.Pin_0, R5.Pin_0, GND_3V3.pin2
  N13: WeMos_D1_Mini1.RX, 5V_GND_RX_TX.pin2
  N14: WeMos_D1_Mini1.TX, 5V_GND_RX_TX.pin1

notes:
  s N S W E F f
