# Fritzing sketch TeenAstroV2.1 (saved by Fritzing 0.9.3b)
circuit board: 10cm x 8cm
breadboards: 2

parts:
  Power_plug_12V = Power plug
  Teensy_3_1_for_Focuser = Teensy 3.1
  Teensy_3_1_for_Telescope = Teensy 3.1
  C3 = Capacitor Polarized [package=cpol-radial-100uf-25v]
  1B_1A_2A_2B = screw terminal, 4 pins
  DS1302 = DS1302 [package="DIP8 [THT]"]
  USB_CONN2 = USB connector [package=THT]
  USB_CONN1 = USB connector [package=THT]
  USB2 = female pin header, 2 pins [form="♀ (female)"]
  Fuse = FUSE [package=fuse_5mm]
  VMot = Screw terminal - 2 pins [package=THT]
  C1 = Capacitor Polarized [package=cpol-radial-100uf-25v]
  D3 = Rectifier Diode 10A [part_number=P1000K]
  12V_to_5V = Voltage Regulator - 5V [package="TO220 [THT]"]
  USB1 = female pin header, 2 pins [form="♀ (female)"]
  TOS-100_Drivers = female pin header, 12 pins [form="♀ (female)"]
  Wifi_ESP_8266 = Generic double row female header - 8 pins [form="♀ (female)" package=THT]
  GND_3_3V_SCL = female pin header, 4 pins [form="♀ (female)"]
  R7 = Resistor [tolerance=±5% resistance=4.7k package=THT]
  R6 = Resistor [tolerance=±5% resistance=4.7k package=THT]
  TMC2100 = Pololu A4988 [package=SO16]
  BAT2 = Battery Holders [package=battcon_12mm_pth]
  5V_to_3V = Voltage Regulator - 3.3V [package="TO220 [THT]"]

nets:
  GND: Power_plug_12V.GND, Teensy_3_1_for_Focuser.GND, Teensy_3_1_for_Telescope.GND, C3.-, DS1302.0V, USB_CONN2.GND, USB_CONN2.chassis5, USB_CONN2.chassis6, USB_CONN1.GND, USB_CONN1.chassis5, USB_CONN1.chassis6, VMot.pin1, C1.-, D3.anode, 12V_to_5V.GND, Wifi_ESP_8266.GND, GND_3_3V_SCL.pin4, TMC2100.ENABLE, TMC2100.GND, BAT2.-, 5V_to_3V.GND
  N1: Power_plug_12V.VCC, Fuse.1
  N2: Teensy_3_1_for_Focuser.D2, DS1302.SCLK_-_SPI_Clock
  N3: Teensy_3_1_for_Focuser.D3, DS1302.I/O_-_SPI_Data_In/Out
  N4: Teensy_3_1_for_Focuser.D4, DS1302.CE_-_Chip_Enable
  N5: Teensy_3_1_for_Focuser.D5, TMC2100.STEP
  N6: Teensy_3_1_for_Focuser.D6, TMC2100.DIR
  N7: Teensy_3_1_for_Focuser.D7, Teensy_3_1_for_Telescope.A8/D22
  N8: Teensy_3_1_for_Focuser.D8, Teensy_3_1_for_Telescope.A7/D21
  VIN: Teensy_3_1_for_Focuser.Vin, Teensy_3_1_for_Telescope.Vin, DS1302.+V, 12V_to_5V.output_voltage, TMC2100.VDD, 5V_to_3V.input_voltage
  N9: Teensy_3_1_for_Telescope.D0, Wifi_ESP_8266.RX
  N10: Teensy_3_1_for_Telescope.D1, Wifi_ESP_8266.TX
  N11: Teensy_3_1_for_Telescope.D2, TOS-100_Drivers.pin1
  N12: Teensy_3_1_for_Telescope.D3, TOS-100_Drivers.pin2
  N13: Teensy_3_1_for_Telescope.D4, TOS-100_Drivers.pin3
  N14: Teensy_3_1_for_Telescope.D5, TOS-100_Drivers.pin4
  N15: Teensy_3_1_for_Telescope.D6, TOS-100_Drivers.pin5
  N16: Teensy_3_1_for_Telescope.D7, TOS-100_Drivers.pin6
  N17: Teensy_3_1_for_Telescope.D8, TOS-100_Drivers.pin7
  N18: Teensy_3_1_for_Telescope.D9, TOS-100_Drivers.pin8
  N19: Teensy_3_1_for_Telescope.D10, TOS-100_Drivers.pin9
  N20: Teensy_3_1_for_Telescope.D11, TOS-100_Drivers.pin10
  N21: Teensy_3_1_for_Telescope.D12, TOS-100_Drivers.pin11
  N22: Teensy_3_1_for_Telescope.VBat, DS1302.Vbat_-_Backup_Supply, BAT2.+
  N23: Teensy_3_1_for_Telescope.D13, TOS-100_Drivers.pin12
  N24: Teensy_3_1_for_Telescope.A4/D18, GND_3_3V_SCL.pin2, R7.Pin_1
  N25: Teensy_3_1_for_Telescope.A5/D19, GND_3_3V_SCL.pin1, R6.Pin_1
  N26: Teensy_3_1_for_Telescope.3V3, GND_3_3V_SCL.pin3, R7.Pin_0, R6.Pin_0
  N27: C3.+, Fuse.2, VMot.pin2, C1.+, D3.cathode, 12V_to_5V.input_voltage, TMC2100.VMOT
  N28: 1B_1A_2A_2B.pin1, TMC2100.1B
  N29: 1B_1A_2A_2B.pin2, TMC2100.1A
  N30: 1B_1A_2A_2B.pin3, TMC2100.2A
  N31: 1B_1A_2A_2B.pin4, TMC2100.2B
  N32: USB_CONN2.d-, USB2.pin2
  N33: USB_CONN2.d+, USB2.pin1
  N34: USB_CONN1.d-, USB1.pin2
  N35: USB_CONN1.d+, USB1.pin1
  N36: Wifi_ESP_8266.VCC, 5V_to_3V.output_voltage

custom parts:
  Generic double row female header - 8 pins: Generic double row female header
