# Fritzing sketch TeenAstroV2.2.Controler.r (saved by Fritzing 0.9.3b)
circuit board: 5cm x 7cm
breadboards: 1

parts:
  J1 = female pin header, 4 pins [form="♀ (female)"]
  J2 = female pin header, 7 pins [form="♀ (female)"]  # not connected
  J3 = female pin header, 8 pins [form="♀ (female)"]
  J4 = female pin header, 3 pins [form="♀ (female)"]  # not connected
  WeMos_D1_Mini1 = WeMos D1 Mini

nets:
  N1: J1.pin1, WeMos_D1_Mini1.5V
  N2: J3.pin1, WeMos_D1_Mini1.3V3
  N3: J3.pin2, WeMos_D1_Mini1.D8
  N4: J3.pin3, WeMos_D1_Mini1.D7
  N5: J3.pin4, WeMos_D1_Mini1.D6
  N6: J3.pin5, WeMos_D1_Mini1.D5
  N7: J3.pin6, WeMos_D1_Mini1.D0
  N8: J3.pin7, WeMos_D1_Mini1.A0
  N9: J3.pin8, WeMos_D1_Mini1.RST
