# Fritzing sketch TeenAstroV2.3 (saved by Fritzing 0.9.3b)
circuit board: 13cm x 15cm
breadboards: 3

parts:
  Power_plug_12V = Power plug
  Teensy_3_1_for_Focuser = Teensy 3.1
  Teensy_3_1_for_Telescope = Teensy 3.1
  C_100uf = Capacitor Polarized [package=cpol-radial-100uf-25v]
  1B_1A_2A_2B = screw terminal, 4 pins
  DS1302 = DS1302 [package="DIP8 [THT]"]
  USB_Telescope = USB connector [package=THT]
  USB_Focuser = USB connector [package=THT]
  USB_Telescope_2 = female pin header, 2 pins [form="♀ (female)"]
  C_100uf_2 = Capacitor Polarized [package=cpol-radial-100uf-25v]
  12V_to_5V = Voltage Regulator - 5V [package="TO220 [THT]"]
  USB_Focuser_2 = female pin header, 2 pins [form="♀ (female)"]
  Right_Ascention = Arduino Uno (Rev3)
  Declination = Arduino Uno (Rev3)
  Battery_20mm = Battery Holders [package=battery_20mm_pth_compact]
  R_array = RPACK* [package=rpack-sip-pth-5]
  LED_F_GND = female pin header, 2 pins [form="♀ (female)"]
  Fuse1 = Fuse with Handler [part_number=Htc-15m]
  Switch = female pin header, 2 pins [form="♀ (female)"]
  TMC2130 = SilentStepStick TMC2130 [package=SO16]
  ST4 = RJ11 Jack [package=rj11-6]
  LED_T_GND = female pin header, 2 pins [form="♀ (female)"]
  RX_TX_GND_5V = female pin header, 4 pins [form="♀ (female)"]
  RX_TX_GND_5V_2 = female pin header, 4 pins [form="♀ (female)"]
  D_A = female pin header, 1 pin [form="♀ (female)"]
  D_K = female pin header, 1 pin [form="♀ (female)"]
  5V_GND = Screw terminal - 2 pins [package=THT]
  X1 = DB9 Connector [package=db9]
  X2 = DB9 Connector [package=db9]
  X3 = DB9 Connector [package=db9]

nets:
  GND: Power_plug_12V.GND, Teensy_3_1_for_Focuser.GND, Teensy_3_1_for_Telescope.GND, C_100uf.-, DS1302.0V, USB_Telescope.GND, USB_Telescope.chassis6, USB_Focuser.GND, USB_Focuser.chassis5, USB_Focuser.chassis6, C_100uf_2.-, 12V_to_5V.GND, Right_Ascention.GND, Declination.GND, Battery_20mm.-, LED_F_GND.pin2, TMC2130.ENABLE, TMC2130.GND, ST4.2, LED_T_GND.pin2, RX_TX_GND_5V.pin2, RX_TX_GND_5V_2.pin2, D_A.pin1, 5V_GND.pin2, X1.6, X1.7, X1.8, X1.9, X2.6, X2.7, X2.8, X2.9
  N1: Power_plug_12V.VCC, Switch.pin1
  N2: Teensy_3_1_for_Focuser.D0, Teensy_3_1_for_Telescope.D10
  N3: Teensy_3_1_for_Focuser.D1, Teensy_3_1_for_Telescope.D9
  N4: Teensy_3_1_for_Focuser.D2, DS1302.SCLK_-_SPI_Clock
  N5: Teensy_3_1_for_Focuser.D3, DS1302.I/O_-_SPI_Data_In/Out
  N6: Teensy_3_1_for_Focuser.D4, DS1302.CE_-_Chip_Enable
  N7: Teensy_3_1_for_Focuser.D6, TMC2130.DIR
  N8: Teensy_3_1_for_Focuser.D7, TMC2130.STEP
  N9: Teensy_3_1_for_Focuser.D10, TMC2130.CS
  N10: Teensy_3_1_for_Focuser.D11, TMC2130.SDI
  N11: Teensy_3_1_for_Focuser.D12, TMC2130.SDO
  N12: Teensy_3_1_for_Focuser.D13, TMC2130.SCK
  N13: Teensy_3_1_for_Focuser.A9/D23, LED_F_GND.pin1
  VIN: Teensy_3_1_for_Focuser.Vin, Teensy_3_1_for_Telescope.Vin, DS1302.+V, 12V_to_5V.output_voltage, Right_Ascention.5V, Declination.5V, R_array.1, TMC2130.VIO, RX_TX_GND_5V.pin1, RX_TX_GND_5V_2.pin1, 5V_GND.pin1, X1.3
  N14: Teensy_3_1_for_Telescope.D0, RX_TX_GND_5V.pin3
  N15: Teensy_3_1_for_Telescope.D1, RX_TX_GND_5V.pin4
  N16: Teensy_3_1_for_Telescope.D2, Right_Ascention.D2
  N17: Teensy_3_1_for_Telescope.D3, Right_Ascention.D4
  N18: Teensy_3_1_for_Telescope.D4, Right_Ascention.D6_PWM
  N19: Teensy_3_1_for_Telescope.D5, Declination.D3_PWM
  N20: Teensy_3_1_for_Telescope.D6, Declination.D5_PWM
  N21: Teensy_3_1_for_Telescope.D7, RX_TX_GND_5V_2.pin4
  N22: Teensy_3_1_for_Telescope.D8, RX_TX_GND_5V_2.pin3
  N23: Teensy_3_1_for_Telescope.D11, Right_Ascention.D11_PWM/MOSI, Declination.D11_PWM/MOSI
  N24: Teensy_3_1_for_Telescope.D12, Right_Ascention.D12/MISO, Declination.D12/MISO
  N25: Teensy_3_1_for_Telescope.VBat, DS1302.Vbat_-_Backup_Supply, Battery_20mm.+
  N26: Teensy_3_1_for_Telescope.D13, Right_Ascention.D13/SCK, Declination.D13/SCK
  N27: Teensy_3_1_for_Telescope.A0/D14, R_array.5, ST4.3
  N28: Teensy_3_1_for_Telescope.A1/D15, R_array.4, ST4.4
  N29: Teensy_3_1_for_Telescope.A2/D16, R_array.3, ST4.5
  N30: Teensy_3_1_for_Telescope.A3/D17, R_array.2, ST4.6
  N31: Teensy_3_1_for_Telescope.A4/D18, Declination.D6_PWM
  N32: Teensy_3_1_for_Telescope.A5/D19, Declination.D4
  N33: Teensy_3_1_for_Telescope.A6/D20, Declination.D2
  N34: Teensy_3_1_for_Telescope.A7/D21, Right_Ascention.D5_PWM
  N35: Teensy_3_1_for_Telescope.A8/D22, Right_Ascention.D3_PWM
  N36: Teensy_3_1_for_Telescope.A9/D23, LED_T_GND.pin1
  VIN_2: C_100uf.+, C_100uf_2.+, 12V_to_5V.input_voltage, Right_Ascention.A0, Right_Ascention.VIN, Declination.A0, Declination.VIN, Fuse1.Connector2, TMC2130.VMOT, D_K.pin1
  N37: 1B_1A_2A_2B.pin1, TMC2130.1B, X3.5
  N38: 1B_1A_2A_2B.pin2, TMC2130.1A, X3.4
  N39: 1B_1A_2A_2B.pin3, TMC2130.2A, X3.2
  N40: 1B_1A_2A_2B.pin4, TMC2130.2B, X3.1
  N41: USB_Telescope.d-, USB_Telescope_2.pin2
  N42: USB_Telescope.d+, USB_Telescope_2.pin1
  N43: USB_Focuser.d-, USB_Focuser_2.pin2
  N44: USB_Focuser.d+, USB_Focuser_2.pin1
  N45: Right_Ascention.D8, X1.2
  N46: Right_Ascention.D9_PWM, X1.4
  N47: Right_Ascention.D10_PWM/SS, X1.5
  N48: Right_Ascention.D7, X1.1
  N49: Declination.D8, X2.4
  N50: Declination.D9_PWM, X2.2
  N51: Declination.D10_PWM/SS, X2.1
  N52: Declination.D7, X2.5
  N53: Fuse1.Connector1, Switch.pin2

custom parts:
  SilentStepStick TMC2130: The TMC2130 provides an integrated motor driver solution for 3D-Printing, Cameras, Scanners and other automated equipment applications. The device has an integrated microstepping indexer, the sensorless stall detection technology StallGuard2™, the sensorless load dependent current control CoolStep™ and the completely noiseless current control mode StealthChop™ and is intended to drive a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
