# Fritzing sketch TeenAstro (saved by Fritzing 0.9.3b)
circuit board: 10cm x 8cm
breadboards: 2

parts:
  TMC2100 = Pololu A4988 [package=SO16]
  Power_plug1 = Power plug
  Teensy_3_1 = Teensy 3.1
  Teensy_3_1_2 = Teensy 3.1
  C1 = Capacitor Polarized [package=cpol-radial-100uf-25v]
  C2 = Capacitor Polarized [package=cpol-radial-100uf-25v]
  C3 = Capacitor Polarized [package=cpol-radial-100uf-25v]
  1B_1A_2A_2B = screw terminal, 4 pins
  R2 = Resistor [tolerance=±5% resistance=10k package="1206 [SMD]"]
  R1 = Resistor [tolerance=±5% resistance=10k package="1206 [SMD]"]
  R3 = Resistor [tolerance=±5% resistance=10k package="1206 [SMD]"]
  R4 = Resistor [tolerance=±5% resistance=10k package="1206 [SMD]"]
  R5 = Resistor [tolerance=±10% resistance=10k package="1206 [SMD]"]
  R6 = Resistor [tolerance=±5% resistance=10k package="1206 [SMD]"]
  R7 = Resistor [tolerance=±5% resistance=10k package="1206 [SMD]"]
  R8 = Resistor [tolerance=±5% resistance=10k package="1206 [SMD]"]
  HdFoc = female pin header, 3 pins [form="♀ (female)"]
  HdCrtlr = female pin header, 7 pins [form="♀ (female)"]
  DS1302 = DS1302 [package="DIP8 [THT]"]
  USB_CONN2 = USB connector [package=THT]
  USB_CONN1 = USB connector [package=THT]
  USB1 = female pin header, 2 pins [form="♀ (female)"]
  USB2 = female pin header, 2 pins [form="♀ (female)"]
  Fuse = FUSE [package=fuse_5mm]
  RA = female pin header, 3 pins [form="♀ (female)"]
  DEC = female pin header, 3 pins [form="♀ (female)"]
  Optional_Digital_Pins = female pin header, 7 pins [form="♀ (female)"]
  VMot = Screw terminal - 2 pins [package=THT]
  12V_to_3_3V = Voltage Regulator - 3.3V [package="TO220 [THT]"]
  3_3V_Gnd = female pin header, 2 pins [form="♀ (female)"]
  BAT2 = Battery Holders [package=battcon_12mm_pth]
  Optional_Analog_Pins = female pin header, 13 pins [form="♀ (female)"]

nets (from the breadboard view):
  GND: TMC2100.ENABLE, TMC2100.GND, Teensy_3_1.GND, C1.-, C2.-, C3.-, R2.Pin_1, R1.Pin_1, DS1302.0V, USB_CONN2.GND, USB_CONN2.chassis5, USB_CONN2.chassis6, USB_CONN1.GND, USB_CONN1.chassis5, USB_CONN1.chassis6, VMot.pin1, 12V_to_3_3V.GND, 3_3V_Gnd.pin2
  N1: TMC2100.STEP, Teensy_3_1.D5
  N2: TMC2100.DIR, Teensy_3_1.D6
  VIN: TMC2100.VDD, Teensy_3_1.Vin, Teensy_3_1_2.Vin, C2.+, HdFoc.pin3, HdCrtlr.pin7, DS1302.+V, Optional_Digital_Pins.pin7, 12V_to_3_3V.output_voltage, 3_3V_Gnd.pin1, Optional_Analog_Pins.pin1
  N3: TMC2100.1B, 1B_1A_2A_2B.pin1
  N4: TMC2100.1A, 1B_1A_2A_2B.pin2
  N5: TMC2100.2A, 1B_1A_2A_2B.pin3
  N6: TMC2100.2B, 1B_1A_2A_2B.pin4
  N7: TMC2100.VMOT, C1.+, C3.+, Fuse.2, VMot.pin2, 12V_to_3_3V.input_voltage
  GND_2: Power_plug1.GND, Teensy_3_1_2.GND, Optional_Digital_Pins.pin1
  N8: Power_plug1.VCC, Fuse.1
  N9: Teensy_3_1.D2, DS1302.SCLK_-_SPI_Clock
  N10: Teensy_3_1.D3, DS1302.I/O_-_SPI_Data_In/Out
  N11: Teensy_3_1.D4, DS1302.CE_-_Chip_Enable
  N12: Teensy_3_1.D7, R1.Pin_0, HdFoc.pin2
  N13: Teensy_3_1.D8, R2.Pin_0, HdFoc.pin1
  N14: Teensy_3_1.A0/D14, Optional_Analog_Pins.pin13
  N15: Teensy_3_1.A1/D15, Optional_Analog_Pins.pin12
  N16: Teensy_3_1.A2/D16, Optional_Analog_Pins.pin11
  N17: Teensy_3_1.A3/D17, Optional_Analog_Pins.pin10
  N18: Teensy_3_1.A4/D18, Optional_Analog_Pins.pin9
  N19: Teensy_3_1.A5/D19, Optional_Analog_Pins.pin8
  N20: Teensy_3_1.A6/D20, Optional_Analog_Pins.pin7
  N21: Teensy_3_1.A7/D21, Optional_Analog_Pins.pin6
  N22: Teensy_3_1.A8/D22, Optional_Analog_Pins.pin5
  N23: Teensy_3_1.A9/D23, Optional_Analog_Pins.pin4
  N24: Teensy_3_1.3V3, Optional_Analog_Pins.pin3
  N25: Teensy_3_1.AGND, Optional_Analog_Pins.pin2
  N26: Teensy_3_1_2.D2, RA.pin3
  N27: Teensy_3_1_2.D3, RA.pin2
  N28: Teensy_3_1_2.D4, RA.pin1
  N29: Teensy_3_1_2.D5, Optional_Digital_Pins.pin6
  N30: Teensy_3_1_2.D6, Optional_Digital_Pins.pin5
  N31: Teensy_3_1_2.D7, Optional_Digital_Pins.pin4
  N32: Teensy_3_1_2.D8, Optional_Digital_Pins.pin3
  N33: Teensy_3_1_2.D9, Optional_Digital_Pins.pin2
  N34: Teensy_3_1_2.D10, DEC.pin3
  N35: Teensy_3_1_2.D11, DEC.pin2
  N36: Teensy_3_1_2.D12, DEC.pin1
  N37: Teensy_3_1_2.VBat, DS1302.Vbat_-_Backup_Supply, BAT2.+
  N38: Teensy_3_1_2.A1/D15, R8.Pin_0, HdCrtlr.pin1
  N39: Teensy_3_1_2.A2/D16, R7.Pin_0, HdCrtlr.pin2
  N40: Teensy_3_1_2.A3/D17, R6.Pin_0, HdCrtlr.pin3
  N41: Teensy_3_1_2.A4/D18, R5.Pin_0, HdCrtlr.pin4
  N42: Teensy_3_1_2.A5/D19, R4.Pin_0, HdCrtlr.pin5
  N43: Teensy_3_1_2.A6/D20, R3.Pin_0, HdCrtlr.pin6
  N44: R3.Pin_1, R4.Pin_1, R5.Pin_1, R6.Pin_1, R7.Pin_1, R8.Pin_1
  N45: USB_CONN2.d-, USB2.pin2
  N46: USB_CONN2.d+, USB2.pin1
  N47: USB_CONN1.d-, USB1.pin2
  N48: USB_CONN1.d+, USB1.pin1
