# Fritzing sketch TeenAstroHandV0.1 (saved by Fritzing 0.9.3b)
circuit board: 5.55cm x 9cm
breadboards: 1

parts:
  C3 = Ceramic Capacitor [capacitance=100nF voltage=35V package="200 mil [THT, multilayer]"]
  C1 = Ceramic Capacitor [capacitance=100nF voltage=35V package="200 mil [THT, multilayer]"]
  C7 = Ceramic Capacitor [capacitance=100nF voltage=35V package="200 mil [THT, multilayer]"]
  C4 = Ceramic Capacitor [capacitance=100nF voltage=35V package="200 mil [THT, multilayer]"]
  C6 = Ceramic Capacitor [capacitance=100nF voltage=35V package="200 mil [THT, multilayer]"]
  C5 = Ceramic Capacitor [capacitance=100nF voltage=35V package="200 mil [THT, multilayer]"]
  C2 = Ceramic Capacitor [capacitance=100nF voltage=35V package="200 mil [THT, multilayer]"]
  R1 = Resistor [tolerance=±5% resistance=220 power=0.25 package=THT]
  R2 = Resistor [tolerance=±5% resistance=220 power=0.25 package=THT]
  R3 = Resistor [tolerance=±5% resistance=220 power=0.25 package=THT]
  R4 = Resistor [tolerance=±5% resistance=220 power=0.25 package=THT]
  R5 = Resistor [tolerance=±5% resistance=220 power=0.25 package=THT]
  R6 = Resistor [tolerance=±5% resistance=220 power=0.25 package=THT]
  R7 = Resistor [tolerance=±5% resistance=220 power=0.25 package=THT]
  5V_GND_SCL_SDA_RST = female pin header, 5 pins [form="♀ (female)"]
  R1_Display = Resistor [tolerance=±5% resistance=220 power=0.25 package=THT]
  R2_Display = Resistor [tolerance=±5% resistance=220 power=0.25 package=THT]
  WeMos_D1_Mini1 = WeMos D1 Mini
  5V_GND_RX_TX = female pin header, 4 pins [form="♀ (female)"]
  J1 = female pin header, 10 pins [form="♀ (female)"]

nets:
  Sud: C3.0, R3.Pin_1, WeMos_D1_Mini1.D6, J1.pin3
  GND: C3.1, C1.1, C7.1, C4.1, C6.1, C5.1, C2.1, R1.Pin_0, R2.Pin_0, R3.Pin_0, R4.Pin_0, R5.Pin_0, 5V_GND_SCL_SDA_RST.pin4, R1_Display.Pin_1, WeMos_D1_Mini1.G, 5V_GND_RX_TX.pin3, J1.pin10
  Shift: C1.0, R1.Pin_1, WeMos_D1_Mini1.D8, J1.pin7
  Fm: C7.0, R7.Pin_1, WeMos_D1_Mini1.D4, J1.pin8
  West: C4.0, R4.Pin_1, WeMos_D1_Mini1.D5, J1.pin5
  Fp: C6.0, R6.Pin_1, WeMos_D1_Mini1.D3, J1.pin9
  East: C5.0, R5.Pin_1, WeMos_D1_Mini1.D0, J1.pin4
  North: C2.0, R2.Pin_1, WeMos_D1_Mini1.D7, J1.pin2
  3v3: R6.Pin_0, R7.Pin_0, R2_Display.Pin_1, WeMos_D1_Mini1.3V3, J1.pin1, J1.pin6
  RST: 5V_GND_SCL_SDA_RST.pin1, WeMos_D1_Mini1.RST
  N1: 5V_GND_SCL_SDA_RST.pin2, WeMos_D1_Mini1.D2
  N2: 5V_GND_SCL_SDA_RST.pin3, WeMos_D1_Mini1.D1
  N3: 5V_GND_SCL_SDA_RST.pin5, WeMos_D1_Mini1.5V, 5V_GND_RX_TX.pin4
  A0: R1_Display.Pin_0, R2_Display.Pin_0, WeMos_D1_Mini1.A0
  N4: WeMos_D1_Mini1.RX, 5V_GND_RX_TX.pin2
  N5: WeMos_D1_Mini1.TX, 5V_GND_RX_TX.pin1

notes:
  GND Fp Fm s 3v3 W E S N 3v3
