# Fritzing sketch TeenAstroHand_DevV0.0 (saved by Fritzing 0.9.3b)
circuit board: 7cm x 12cm
breadboards: 1

parts:
  C3 = Ceramic Capacitor [capacitance=100nF voltage=35V package="200 mil [THT, multilayer]"]
  C1 = Ceramic Capacitor [capacitance=100nF voltage=35V package="200 mil [THT, multilayer]"]
  C7 = Ceramic Capacitor [capacitance=100nF voltage=35V package="200 mil [THT, multilayer]"]
  C4 = Ceramic Capacitor [capacitance=100nF voltage=35V package="200 mil [THT, multilayer]"]
  C6 = Ceramic Capacitor [capacitance=100nF voltage=35V package="200 mil [THT, multilayer]"]
  C5 = Ceramic Capacitor [capacitance=100nF voltage=35V package="200 mil [THT, multilayer]"]
  C2 = Ceramic Capacitor [capacitance=100nF voltage=35V package="200 mil [THT, multilayer]"]
  R1 = Resistor [tolerance=±5% resistance=220 power=0.25 package=THT]
  R2 = Resistor [tolerance=±5% resistance=220 power=0.25 package=THT]
  R3 = Resistor [tolerance=±5% resistance=220 power=0.25 package=THT]
  R4 = Resistor [tolerance=±5% resistance=220 power=0.25 package=THT]
  R5 = Resistor [tolerance=±5% resistance=220 power=0.25 package=THT]
  R6 = Resistor [tolerance=±5% resistance=220 power=0.25 package=THT]
  R7 = Resistor [tolerance=±5% resistance=220 power=0.25 package=THT]
  5V_GND_SCL_SDA_RST = female pin header, 5 pins [form="♀ (female)"]
  R1_Disp = Resistor [tolerance=±5% resistance=220 power=0.25 package=THT]
  Ri_Disp = Resistor [tolerance=±5% resistance=220 power=0.25 package=THT]
  WeMos_D1_Mini1 = WeMos D1 Mini
  5V_GND_RX_TX = female pin header, 4 pins [form="♀ (female)"]
  Ss = Pushbutton [package="[THT]"]
  Sfm = Pushbutton [package="[THT]"]
  Sfp = Pushbutton [package="[THT]"]
  Rj_Disp = Resistor [tolerance=±5% resistance=220 power=0.25 package=THT]
  Rk_Disp = Resistor [tolerance=±5% resistance=220 power=0.25 package=THT]
  J1 = double row male pin header, 6 pins [form="♂ (male)"]
  SN = Pushbutton [package="[THT]"]
  SW = Pushbutton [package="[THT]"]
  SE = Pushbutton [package="[THT]"]
  SS = Pushbutton [package="[THT]"]

nets:
  Sud: C3.0, R3.Pin_1, WeMos_D1_Mini1.D6, SS.Pin_1, SS.Pin_2
  GND: C3.1, C1.1, C7.1, C4.1, C6.1, C5.1, C2.1, R1.Pin_0, R2.Pin_0, R3.Pin_0, R4.Pin_0, R5.Pin_0, 5V_GND_SCL_SDA_RST.pin4, R1_Disp.Pin_1, WeMos_D1_Mini1.G, 5V_GND_RX_TX.pin3, Sfm.Pin_3, Sfm.Pin_4, Sfp.Pin_3, Sfp.Pin_4
  Shift: C1.0, R1.Pin_1, WeMos_D1_Mini1.D8, Ss.Pin_1, Ss.Pin_2
  Fm: C7.0, R7.Pin_1, WeMos_D1_Mini1.D4, Sfm.Pin_1, Sfm.Pin_2
  West: C4.0, R4.Pin_1, WeMos_D1_Mini1.D5, SW.Pin_1, SW.Pin_2
  Fp: C6.0, R6.Pin_1, WeMos_D1_Mini1.D3, Sfp.Pin_1, Sfp.Pin_2
  East: C5.0, R5.Pin_1, WeMos_D1_Mini1.D0, SE.Pin_1, SE.Pin_2
  North: C2.0, R2.Pin_1, WeMos_D1_Mini1.D7, SN.Pin_1, SN.Pin_2
  3v3: R6.Pin_0, R7.Pin_0, WeMos_D1_Mini1.3V3, Ss.Pin_3, Ss.Pin_4, J1.pin1, J1.pin2, J1.pin3, SN.Pin_3, SN.Pin_4, SW.Pin_3, SW.Pin_4, SE.Pin_3, SE.Pin_4, SS.Pin_3, SS.Pin_4
  RST: 5V_GND_SCL_SDA_RST.pin1, WeMos_D1_Mini1.RST
  N1: 5V_GND_SCL_SDA_RST.pin2, WeMos_D1_Mini1.D2
  N2: 5V_GND_SCL_SDA_RST.pin3, WeMos_D1_Mini1.D1
  N3: 5V_GND_SCL_SDA_RST.pin5, WeMos_D1_Mini1.5V, 5V_GND_RX_TX.pin4
  A0: R1_Disp.Pin_0, Ri_Disp.Pin_0, WeMos_D1_Mini1.A0, Rj_Disp.Pin_0, Rk_Disp.Pin_0
  Ri: Ri_Disp.Pin_1, J1.pin4
  N4: WeMos_D1_Mini1.RX, 5V_GND_RX_TX.pin2
  N5: WeMos_D1_Mini1.TX, 5V_GND_RX_TX.pin1
  Rj: Rj_Disp.Pin_1, J1.pin5
  Rk: Rk_Disp.Pin_1, J1.pin6
