# Fritzing sketch TeenAstroMiniFocuserV2.4.1_db9 (saved by Fritzing 0.9.3b)
circuit board: 7.5cm x 10cm
breadboards: 5

parts:
  Teensy_3_2_for_Telescope = Teensy 3.1
  USB_Focuser = USB connector [package=THT]
  USB_Telescope = female pin header, 2 pins [form="♀ (female)"]
  LED_GND = female pin header, 2 pins [form="♀ (female)"]
  J2 = female pin header, 11 pins [form="♀ (female)"]
  J4 = female pin header, 11 pins [form="♀ (female)"]
  TMC_5160 = female pin header, 11 pins [form="♀ (female)"]
  TMC_5160_2 = female pin header, 11 pins [form="♀ (female)"]
  FOC_1 = DB9 Connector [package=db9]
  FOC_2 = DB9 Connector [package=db9]
  TMC2130 = SilentStepStick TMC2130 [package=SO16]
  TMC2130_2 = SilentStepStick TMC2130 [package=SO16]
  RX3_TX3_RX2_TX2 = female pin header, 4 pins [form="♀ (female)"]
  VMOT_5v_VBAT_GND = female pin header, 4 pins [form="♀ (female)"]
  C_180uF = Capacitor Polarized [package=cpol-radial-100uf-25v]
  C_180uF_2 = Capacitor Polarized [package=cpol-radial-100uf-25v]
  IC1 = DS1302 [package="DIP8 [THT]"]

nets:
  GND: Teensy_3_2_for_Telescope.GND, USB_Focuser.GND, LED_GND.pin2, J2.pin2, J2.pin7, J4.pin2, J4.pin7, TMC_5160.pin2, TMC_5160.pin7, TMC_5160.pin8, TMC_5160_2.pin2, TMC_5160_2.pin7, TMC_5160_2.pin8, FOC_1.6, TMC2130.GND, TMC2130_2.GND, VMOT_5v_VBAT_GND.pin4, C_180uF.-, C_180uF_2.-
  N1: Teensy_3_2_for_Telescope.D2, TMC_5160_2.pin11, TMC2130_2.DIR
  N2: Teensy_3_2_for_Telescope.D3, TMC_5160_2.pin9, TMC2130_2.ENABLE
  N3: Teensy_3_2_for_Telescope.D4, TMC_5160.pin11, TMC2130.DIR
  N4: Teensy_3_2_for_Telescope.D5, TMC_5160.pin9, TMC2130.ENABLE
  N5: Teensy_3_2_for_Telescope.D7, RX3_TX3_RX2_TX2.pin1
  N6: Teensy_3_2_for_Telescope.D8, RX3_TX3_RX2_TX2.pin2
  N7: Teensy_3_2_for_Telescope.D9, RX3_TX3_RX2_TX2.pin3
  N8: Teensy_3_2_for_Telescope.D10, RX3_TX3_RX2_TX2.pin4
  N9: Teensy_3_2_for_Telescope.D11, TMC_5160.pin5, TMC_5160_2.pin5, TMC2130.SDO, TMC2130_2.SDO
  N10: Teensy_3_2_for_Telescope.D12, TMC_5160.pin6, TMC_5160_2.pin6, TMC2130.SDI, TMC2130_2.SDI
  N11: Teensy_3_2_for_Telescope.VBat, VMOT_5v_VBAT_GND.pin3, IC1.Vbat_-_Backup_Supply
  N12: Teensy_3_2_for_Telescope.D13, TMC_5160.pin4, TMC_5160_2.pin4, TMC2130.CS, TMC2130_2.CS
  N13: Teensy_3_2_for_Telescope.A5/D19, TMC_5160.pin3, TMC2130.SCK
  N14: Teensy_3_2_for_Telescope.A6/D20, TMC_5160.pin10, TMC2130.STEP
  N15: Teensy_3_2_for_Telescope.A7/D21, TMC_5160_2.pin3, TMC2130_2.SCK
  N16: Teensy_3_2_for_Telescope.A8/D22, TMC_5160_2.pin10, TMC2130_2.STEP
  N17: Teensy_3_2_for_Telescope.Vin, TMC_5160.pin1, TMC_5160_2.pin1, TMC2130.VIO, TMC2130_2.VIO, VMOT_5v_VBAT_GND.pin2, IC1.+V
  N18: USB_Focuser.d-, USB_Telescope.pin2
  N19: USB_Focuser.d+, USB_Telescope.pin1
  N20: J2.pin1, J4.pin1, TMC2130.VMOT, TMC2130_2.VMOT, VMOT_5v_VBAT_GND.pin1, C_180uF.+, C_180uF_2.+
  N21: J2.pin3, FOC_1.1, TMC2130_2.2B
  N22: J2.pin4, FOC_1.2, TMC2130_2.2A
  N23: J2.pin5, FOC_1.4, TMC2130_2.1A
  N24: J2.pin6, FOC_1.5, TMC2130_2.1B
  N25: J4.pin3, FOC_2.1, TMC2130.2B
  N26: J4.pin4, FOC_2.2, TMC2130.2A
  N27: J4.pin5, FOC_2.4, TMC2130.1A
  N28: J4.pin6, FOC_2.5, TMC2130.1B

notes:
  D+ D-
  REFL
  DRV_EN
  CLK16
  GND
  SDO
  SDI
  SCK
  CSN
  VCC_IO
  REFR

custom parts:
  SilentStepStick TMC2130: The TMC2130 provides an integrated motor driver solution for 3D-Printing, Cameras, Scanners and other automated equipment applications. The device has an integrated microstepping indexer, the sensorless stall detection technology StallGuard2™, the sensorless load dependent current control CoolStep™ and the completely noiseless current control mode StealthChop™ and is intended to drive a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
