# Fritzing sketch TeenAstroMiniV2.4.2_db9 (saved by Fritzing 0.9.3b)
circuit board: 7.5cm x 10cm
breadboards: 5

parts:
  Power_plug_12V = Power plug
  Teensy_3_2_for_Telescope = Teensy 3.1
  USB_Telescope = USB connector [package=THT]
  USB_Telescope_2 = female pin header, 2 pins [form="♀ (female)"]
  12V_to_5V = Voltage Regulator - 5V [package="TO220 [THT]"]
  Battery_20mm = Battery Holders [package=battery_20mm_pth_compact]
  R_array = RPACK* [package=rpack-sip-pth-5]
  Switch = female pin header, 2 pins [form="♀ (female)"]
  ST4 = RJ11 Jack [package=rj11-6]
  RX_TX_GND_5V = female pin header, 4 pins [form="♀ (female)"]
  LED_GND = female pin header, 2 pins [form="♀ (female)"]
  J2 = female pin header, 11 pins [form="♀ (female)"]
  J4 = female pin header, 11 pins [form="♀ (female)"]
  TMC_5160 = female pin header, 11 pins [form="♀ (female)"]
  TMC_5160_2 = female pin header, 11 pins [form="♀ (female)"]
  Fuse1 = Fuse with Handler [part_number=Htc-15m]
  RA = DB9 Connector [package=db9]
  DEC = DB9 Connector [package=db9]
  D_K = female pin header, 1 pin [form="♀ (female)"]
  D_A = female pin header, 1 pin [form="♀ (female)"]
  TMC2130 = SilentStepStick TMC2130 [package=SO16]
  TMC2130_2 = SilentStepStick TMC2130 [package=SO16]
  RX3_TX3_RX2_TX2 = female pin header, 4 pins [form="♀ (female)"]
  VMOT_5v_VBAT_GND = female pin header, 4 pins [form="♀ (female)"]
  C_100uf = Capacitor Polarized [package=cpol-radial-100uf-25v]
  C_180uF = Capacitor Polarized [package=cpol-radial-100uf-25v]
  C_180uF_2 = Capacitor Polarized [package=cpol-radial-100uf-25v]

nets:
  GND: Power_plug_12V.GND, Teensy_3_2_for_Telescope.GND, USB_Telescope.GND, USB_Telescope.chassis5, USB_Telescope.chassis6, 12V_to_5V.GND, Battery_20mm.-, ST4.2, RX_TX_GND_5V.pin3, LED_GND.pin2, J2.pin2, J2.pin7, J4.pin2, J4.pin7, TMC_5160.pin2, TMC_5160.pin7, TMC_5160.pin8, TMC_5160_2.pin2, TMC_5160_2.pin7, TMC_5160_2.pin8, RA.6, D_A.pin1, TMC2130.GND, TMC2130_2.GND, VMOT_5v_VBAT_GND.pin4, C_100uf.-, C_180uF.-, C_180uF_2.-
  N1: Power_plug_12V.VCC, Switch.pin1
  N2: Teensy_3_2_for_Telescope.D0, RX_TX_GND_5V.pin2
  N3: Teensy_3_2_for_Telescope.D1, RX_TX_GND_5V.pin1
  N4: Teensy_3_2_for_Telescope.D2, TMC_5160_2.pin11, TMC2130_2.DIR
  N5: Teensy_3_2_for_Telescope.D3, TMC_5160_2.pin9, TMC2130_2.ENABLE
  N6: Teensy_3_2_for_Telescope.D4, TMC_5160.pin11, TMC2130.DIR
  N7: Teensy_3_2_for_Telescope.D5, TMC_5160.pin9, TMC2130.ENABLE
  N8: Teensy_3_2_for_Telescope.D6, RA.3
  N9: Teensy_3_2_for_Telescope.D7, RX3_TX3_RX2_TX2.pin1
  N10: Teensy_3_2_for_Telescope.D8, RX3_TX3_RX2_TX2.pin2
  N11: Teensy_3_2_for_Telescope.D9, RX3_TX3_RX2_TX2.pin3
  N12: Teensy_3_2_for_Telescope.D10, RX3_TX3_RX2_TX2.pin4
  N13: Teensy_3_2_for_Telescope.D11, TMC_5160.pin5, TMC_5160_2.pin5, TMC2130.SDO, TMC2130_2.SDO
  N14: Teensy_3_2_for_Telescope.D12, TMC_5160.pin6, TMC_5160_2.pin6, TMC2130.SDI, TMC2130_2.SDI
  N15: Teensy_3_2_for_Telescope.VBat, Battery_20mm.+, VMOT_5v_VBAT_GND.pin3
  N16: Teensy_3_2_for_Telescope.D13, TMC_5160.pin4, TMC_5160_2.pin4, TMC2130.CS, TMC2130_2.CS
  N17: Teensy_3_2_for_Telescope.A0/D14, R_array.5, ST4.3
  N18: Teensy_3_2_for_Telescope.A1/D15, R_array.4, ST4.4
  N19: Teensy_3_2_for_Telescope.A2/D16, R_array.3, ST4.5
  N20: Teensy_3_2_for_Telescope.A3/D17, R_array.2, ST4.6
  N21: Teensy_3_2_for_Telescope.A5/D19, TMC_5160.pin3, TMC2130.SCK
  N22: Teensy_3_2_for_Telescope.A6/D20, TMC_5160.pin10, TMC2130.STEP
  N23: Teensy_3_2_for_Telescope.A7/D21, TMC_5160_2.pin3, TMC2130_2.SCK
  N24: Teensy_3_2_for_Telescope.A8/D22, TMC_5160_2.pin10, TMC2130_2.STEP
  N25: Teensy_3_2_for_Telescope.A9/D23, LED_GND.pin1
  N26: Teensy_3_2_for_Telescope.Vin, 12V_to_5V.output_voltage, R_array.1, RX_TX_GND_5V.pin4, TMC_5160.pin1, TMC_5160_2.pin1, TMC2130.VIO, TMC2130_2.VIO, VMOT_5v_VBAT_GND.pin2
  N27: USB_Telescope.d-, USB_Telescope_2.pin2
  N28: USB_Telescope.d+, USB_Telescope_2.pin1
  N29: 12V_to_5V.input_voltage, J2.pin1, J4.pin1, Fuse1.Connector2, D_K.pin1, TMC2130.VMOT, TMC2130_2.VMOT, VMOT_5v_VBAT_GND.pin1, C_100uf.+, C_180uF.+, C_180uF_2.+
  N30: Switch.pin2, Fuse1.Connector1
  N31: J2.pin3, RA.1, TMC2130_2.2B
  N32: J2.pin4, RA.2, TMC2130_2.2A
  N33: J2.pin5, RA.4, TMC2130_2.1A
  N34: J2.pin6, RA.5, TMC2130_2.1B
  N35: J2.pin9, RA.7
  N36: J2.pin10, RA.8
  N37: J2.pin11, RA.9
  N38: J4.pin3, DEC.1, TMC2130.2B
  N39: J4.pin4, DEC.2, TMC2130.2A
  N40: J4.pin5, DEC.4, TMC2130.1A
  N41: J4.pin6, DEC.5, TMC2130.1B
  N42: J4.pin9, DEC.7
  N43: J4.pin10, DEC.8
  N44: J4.pin11, DEC.9

notes:
  D+ D-
  REFL
  DRV_EN
  CLK16
  GND
  SDO
  SDI
  SCK
  CSN
  VCC_IO
  REFR

custom parts:
  SilentStepStick TMC2130: The TMC2130 provides an integrated motor driver solution for 3D-Printing, Cameras, Scanners and other automated equipment applications. The device has an integrated microstepping indexer, the sensorless stall detection technology StallGuard2™, the sensorless load dependent current control CoolStep™ and the completely noiseless current control mode StealthChop™ and is intended to drive a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
