# Fritzing sketch TeenAstroMiniV2.5.0_db9 (saved by Fritzing 0.9.3b)
circuit board: 7.5cm x 10cm
breadboards: 5

parts:
  Power_plug_12V = Power plug
  Teensy_4_0_for_Telescope = Teensy 3.1
  USB_Telescope = USB connector [package=THT]
  Battery_20mm = Battery Holders [package=battery_20mm_pth_compact]
  R_array = RPACK* [package=rpack-sip-pth-5]
  Switch = female pin header, 2 pins [form="♀ (female)"]
  Fuse1 = Fuse with Handler [part_number=Htc-15m]
  RA = DB9 Connector [package=db9]
  DEC = DB9 Connector [package=db9]
  D_K = female pin header, 1 pin [form="♀ (female)"]
  D_A = female pin header, 1 pin [form="♀ (female)"]
  TMC2130 = SilentStepStick TMC2130 [package=SO16]
  TMC2130_2 = SilentStepStick TMC2130 [package=SO16]
  RX3_TX3_RX2_TX2 = female pin header, 4 pins [form="♀ (female)"]
  C_100uf = Capacitor Polarized [package=cpol-radial-100uf-25v]
  C_180uF = Capacitor Polarized [package=cpol-radial-100uf-25v]
  C_180uF_2 = Capacitor Polarized [package=cpol-radial-100uf-25v]
  ST4 = RJ11 Jack [package=rj11-6]
  A2_B2_A1_B1 = female pin header, 4 pins [form="♀ (female)"]
  VMOT_5v_VBAT_GND = female pin header, 4 pins [form="♀ (female)"]
  TMC_5160 = female pin header, 11 pins [form="♀ (female)"]
  J2 = female pin header, 11 pins [form="♀ (female)"]
  J4 = female pin header, 11 pins [form="♀ (female)"]
  D+_D- = female pin header, 2 pins [form="♀ (female)"]
  J6 = female pin header, 8 pins [form="♀ (female)"]
  J7 = female pin header, 8 pins [form="♀ (female)"]
  U1 = Voltage Regulator [package=to220-igo]
  TX1_RX1_GND_5V = female pin header, 4 pins [form="♀ (female)"]
  LED_GND = female pin header, 2 pins [form="♀ (female)"]
  TMC_5160_2 = female pin header, 11 pins [form="♀ (female)"]

nets:
  N1: Power_plug_12V.VCC, Switch.pin1
  GND: Power_plug_12V.GND, Teensy_4_0_for_Telescope.GND, USB_Telescope.GND, USB_Telescope.chassis6, Battery_20mm.-, RA.6, DEC.6, D_A.pin1, TMC2130.GND, TMC2130_2.GND, C_100uf.-, C_180uF_2.-, ST4.2, VMOT_5v_VBAT_GND.pin4, TMC_5160.pin2, TMC_5160.pin7, TMC_5160.pin8, J2.pin2, J2.pin7, J4.pin2, J4.pin7, J6.pin2, J6.pin4, J6.pin6, J6.pin8, U1.GND, TX1_RX1_GND_5V.pin3, LED_GND.pin2, TMC_5160_2.pin2, TMC_5160_2.pin7, TMC_5160_2.pin8
  N2: Teensy_4_0_for_Telescope.D0, TX1_RX1_GND_5V.pin2
  N3: Teensy_4_0_for_Telescope.D1, TX1_RX1_GND_5V.pin1
  N4: Teensy_4_0_for_Telescope.D2, TMC2130_2.DIR, TMC_5160.pin11
  N5: Teensy_4_0_for_Telescope.D3, TMC2130_2.ENABLE, TMC_5160.pin9
  N6: Teensy_4_0_for_Telescope.D4, TMC2130.DIR, TMC_5160_2.pin11
  N7: Teensy_4_0_for_Telescope.D5, TMC2130.ENABLE, TMC_5160_2.pin9
  N8: Teensy_4_0_for_Telescope.D6, RA.3
  N9: Teensy_4_0_for_Telescope.D7, RX3_TX3_RX2_TX2.pin3
  N10: Teensy_4_0_for_Telescope.D8, RX3_TX3_RX2_TX2.pin4
  N11: Teensy_4_0_for_Telescope.D9, TMC2130_2.SCK, TMC_5160.pin3
  N12: Teensy_4_0_for_Telescope.D10, TMC2130.SCK, TMC_5160_2.pin3
  N13: Teensy_4_0_for_Telescope.D11, TMC2130.SDO, TMC2130_2.SDO, TMC_5160.pin5, TMC_5160_2.pin5
  N14: Teensy_4_0_for_Telescope.D12, TMC2130.SDI, TMC2130_2.SDI, TMC_5160.pin6, TMC_5160_2.pin6
  N15: Teensy_4_0_for_Telescope.VBat, Battery_20mm.+, VMOT_5v_VBAT_GND.pin3
  N16: Teensy_4_0_for_Telescope.D13, TMC2130.CS, TMC2130_2.CS, TMC_5160.pin4, TMC_5160_2.pin4
  N17: Teensy_4_0_for_Telescope.A0/D14, RX3_TX3_RX2_TX2.pin2
  N18: Teensy_4_0_for_Telescope.A1/D15, RX3_TX3_RX2_TX2.pin1
  N19: Teensy_4_0_for_Telescope.A2/D16, R_array.5, ST4.3
  N20: Teensy_4_0_for_Telescope.A3/D17, R_array.4, ST4.4
  N21: Teensy_4_0_for_Telescope.A4/D18, R_array.3, ST4.5
  N22: Teensy_4_0_for_Telescope.A5/D19, R_array.2, ST4.6
  N23: Teensy_4_0_for_Telescope.A6/D20, TMC2130.STEP, TMC_5160_2.pin10
  N24: Teensy_4_0_for_Telescope.A7/D21, DEC.3
  N25: Teensy_4_0_for_Telescope.A8/D22, TMC2130_2.STEP, TMC_5160.pin10
  N26: Teensy_4_0_for_Telescope.A9/D23, LED_GND.pin1
  N27: Teensy_4_0_for_Telescope.3V3, R_array.1
  N28: Teensy_4_0_for_Telescope.Vin, RA.7, DEC.7, TMC2130.VIO, TMC2130_2.VIO, VMOT_5v_VBAT_GND.pin2, TMC_5160.pin1, U1.OUT, TX1_RX1_GND_5V.pin4, TMC_5160_2.pin1
  N29: USB_Telescope.d-, D+_D-.pin2
  N30: USB_Telescope.d+, D+_D-.pin1
  N31: Switch.pin2, Fuse1.Connector1
  VM: Fuse1.Connector2, D_K.pin1, TMC2130.VMOT, TMC2130_2.VMOT, C_100uf.+, C_180uF.+, C_180uF_2.+, VMOT_5v_VBAT_GND.pin1, J2.pin1, J4.pin1, U1.IN
  M2B_A1: RA.1, TMC2130_2.2B, J2.pin3
  M2A_A1: RA.2, TMC2130_2.2A, J2.pin4
  M1A_A1: RA.4, TMC2130_2.1A, J2.pin5
  M1B_A1: RA.5, TMC2130_2.1B, J2.pin6
  N32: RA.8, J7.pin4
  N33: RA.9, J7.pin2
  M2B_A2: DEC.1, TMC2130.2B, J4.pin3
  M2A_A2: DEC.2, TMC2130.2A, J4.pin4
  M1A_A2: DEC.4, TMC2130.1A, J4.pin5
  M1B_A2: DEC.5, TMC2130.1B, J4.pin6
  N34: DEC.8, J7.pin8
  N35: DEC.9, J7.pin6
  N36: A2_B2_A1_B1.pin1, J6.pin1, J7.pin1
  N37: A2_B2_A1_B1.pin2, J6.pin3, J7.pin3
  N38: A2_B2_A1_B1.pin3, J6.pin5, J7.pin5
  N39: A2_B2_A1_B1.pin4, J6.pin7, J7.pin7

notes:
  REFL
  DRV_EN
  CLK16
  GND
  SDO
  SDI
  SCK
  CSN
  VCC_IO
  REFR
  SHC

custom parts:
  SilentStepStick TMC2130: The TMC2130 provides an integrated motor driver solution for 3D-Printing, Cameras, Scanners and other automated equipment applications. The device has an integrated microstepping indexer, the sensorless stall detection technology StallGuard2™, the sensorless load dependent current control CoolStep™ and the completely noiseless current control mode StealthChop™ and is intended to drive a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
