# Fritzing sketch TeenAstroV2.5.0 (saved by Fritzing 0.9.3b)
circuit board: 13cm x 15cm
breadboards: 7

parts:
  Power_plug_12V = Power plug
  Teensy_3_2_for_Focuser = Teensy 3.1
  Teensy_4_0_for_telescope = Teensy 3.1
  DS1302 = DS1302 [package="DIP8 [THT]"]
  USB_Telescope = USB connector [package=THT]
  USB_Focuser = USB connector [package=THT]
  USB_Telescope_2 = female pin header, 2 pins [form="♀ (female)"]
  C_100uf = Capacitor Polarized [package=cpol-radial-100uf-25v]
  12V_to_5V = Voltage Regulator - 5V [package="TO220 [THT]"]
  USB_Focuser_2 = female pin header, 2 pins [form="♀ (female)"]
  Battery_20mm = Battery Holders [package=battery_20mm_pth_compact]
  R_array = RPACK* [package=rpack-sip-pth-5]
  Fuse1 = Fuse with Handler [part_number=Htc-15m]
  Switch = female pin header, 2 pins [form="♀ (female)"]
  ST4 = RJ11 Jack [package=rj11-6]
  D_A = female pin header, 1 pin [form="♀ (female)"]  # not connected
  D_K = female pin header, 1 pin [form="♀ (female)"]
  X1 = DB9 Connector [package=db9]
  X2 = DB9 Connector [package=db9]
  X3 = DB9 Connector [package=db9]
  LED_F_T_GND = female pin header, 3 pins [form="♀ (female)"]
  J1 = female pin header, 11 pins [form="♀ (female)"]
  J2 = female pin header, 11 pins [form="♀ (female)"]
  J3 = female pin header, 11 pins [form="♀ (female)"]
  J4 = female pin header, 11 pins [form="♀ (female)"]
  TMC2130_RA = SilentStepStick TMC2130 [package=SO16]
  TMC2130_DEC = SilentStepStick TMC2130 [package=SO16]
  J5 = female pin header, 11 pins [form="♀ (female)"]
  J6 = female pin header, 11 pins [form="♀ (female)"]
  TMC2130_FOC = SilentStepStick TMC2130 [package=SO16]
  EN_EA_EB_X_A1_A2_B1_B2 = screw terminal, 8 pins
  EN_EA_EB_X_A1_A2_B1_B2_2 = screw terminal, 8 pins
  EN_EA_EB_X_A1_A2_B1_B2_3 = screw terminal, 8 pins
  C_150uf_LOWESR = Capacitor Polarized [package=cpol-radial-100uf-25v]
  C_150uf_LOWESR_2 = Capacitor Polarized [package=cpol-radial-100uf-25v]
  C_150uf_LOWESR_3 = Capacitor Polarized [package=cpol-radial-100uf-25v]
  R_Pull_Foc_4_7k = Resistor [tolerance=±5% resistance=4.7k package=THT]
  RX_TX_GND_5V = female pin header, 4 pins [form="♀ (female)"]
  PPS_TX_RX_GND_5V = double row female pin header, 10 pins [form="♀ (female)"]

nets (from the pcb view):
  N1: Power_plug_12V.VCC, Switch.pin1
  N2: Teensy_3_2_for_Focuser.D0, Teensy_4_0_for_telescope.A0/D14
  N3: Teensy_3_2_for_Focuser.D1, Teensy_4_0_for_telescope.A1/D15
  N4: Teensy_3_2_for_Focuser.D2, DS1302.SCLK_-_SPI_Clock
  N5: Teensy_3_2_for_Focuser.D3, DS1302.I/O_-_SPI_Data_In/Out
  N6: Teensy_3_2_for_Focuser.D4, DS1302.CE_-_Chip_Enable
  N7: Teensy_3_2_for_Focuser.D9, X3.7, R_Pull_Foc_4_7k.Pin_1
  N8: Teensy_3_2_for_Focuser.D10, J6.pin3, TMC2130_FOC.SCK
  N9: Teensy_3_2_for_Focuser.D11, J6.pin5, TMC2130_FOC.SDO
  N10: Teensy_3_2_for_Focuser.D12, J6.pin6, TMC2130_FOC.SDI
  N11: Teensy_3_2_for_Focuser.D13, J6.pin4, TMC2130_FOC.CS
  N12: Teensy_3_2_for_Focuser.A6/D20, J6.pin9, TMC2130_FOC.ENABLE
  N13: Teensy_3_2_for_Focuser.A7/D21, J6.pin10, TMC2130_FOC.STEP
  N14: Teensy_3_2_for_Focuser.A8/D22, J6.pin11, TMC2130_FOC.DIR
  N15: Teensy_3_2_for_Focuser.A9/D23, LED_F_T_GND.pin3
  VIN: Teensy_3_2_for_Focuser.Vin, Teensy_4_0_for_telescope.Vin, DS1302.+V, 12V_to_5V.output_voltage, X3.6, J1.pin1, J3.pin1, TMC2130_RA.VIO, TMC2130_DEC.VIO, J6.pin1, TMC2130_FOC.VIO, R_Pull_Foc_4_7k.Pin_0, RX_TX_GND_5V.pin1, PPS_TX_RX_GND_5V.pin1, PPS_TX_RX_GND_5V.pin10
  N16: Teensy_4_0_for_telescope.D0, RX_TX_GND_5V.pin3
  N17: Teensy_4_0_for_telescope.D1, RX_TX_GND_5V.pin4
  N18: Teensy_4_0_for_telescope.D2, J1.pin11, TMC2130_RA.DIR
  N19: Teensy_4_0_for_telescope.D3, J1.pin9, TMC2130_RA.ENABLE
  N20: Teensy_4_0_for_telescope.D4, J3.pin11, TMC2130_DEC.DIR
  N21: Teensy_4_0_for_telescope.D5, J3.pin9, TMC2130_DEC.ENABLE
  N22: Teensy_4_0_for_telescope.D6, X1.3
  N23: Teensy_4_0_for_telescope.D7, PPS_TX_RX_GND_5V.pin3, PPS_TX_RX_GND_5V.pin7
  N24: Teensy_4_0_for_telescope.D8, PPS_TX_RX_GND_5V.pin4, PPS_TX_RX_GND_5V.pin8
  N25: Teensy_4_0_for_telescope.D9, R_array.4, ST4.4
  N26: Teensy_4_0_for_telescope.D10, R_array.5, ST4.3
  N27: Teensy_4_0_for_telescope.D11, J1.pin5, J3.pin5, TMC2130_RA.SDO, TMC2130_DEC.SDO
  N28: Teensy_4_0_for_telescope.D12, J1.pin6, J3.pin6, TMC2130_RA.SDI, TMC2130_DEC.SDI
  N29: Teensy_4_0_for_telescope.VBat, DS1302.Vbat_-_Backup_Supply, Battery_20mm.+
  N30: Teensy_4_0_for_telescope.D13, J1.pin4, J3.pin4, TMC2130_RA.CS, TMC2130_DEC.CS
  N31: Teensy_4_0_for_telescope.A2/D16, R_array.3, ST4.5
  N32: Teensy_4_0_for_telescope.A3/D17, R_array.2, ST4.6
  N33: Teensy_4_0_for_telescope.A4/D18, PPS_TX_RX_GND_5V.pin5, PPS_TX_RX_GND_5V.pin6
  N34: Teensy_4_0_for_telescope.A5/D19, J3.pin3, TMC2130_DEC.SCK
  N35: Teensy_4_0_for_telescope.A6/D20, J3.pin10, TMC2130_DEC.STEP
  N36: Teensy_4_0_for_telescope.A7/D21, J1.pin3, TMC2130_RA.SCK
  N37: Teensy_4_0_for_telescope.A8/D22, J1.pin10, TMC2130_RA.STEP
  N38: Teensy_4_0_for_telescope.A9/D23, LED_F_T_GND.pin2
  N39: Teensy_4_0_for_telescope.3V3, R_array.1
  N40: USB_Telescope.d-, USB_Telescope_2.pin2
  N41: USB_Telescope.d+, USB_Telescope_2.pin1
  GND: USB_Telescope.GND, USB_Telescope.chassis6, USB_Focuser.GND, USB_Focuser.chassis5, USB_Focuser.chassis6
  N42: USB_Focuser.d-, USB_Focuser_2.pin2
  N43: USB_Focuser.d+, USB_Focuser_2.pin1
  N44: C_100uf.+, 12V_to_5V.input_voltage, Fuse1.Connector2, D_K.pin1, J2.pin1, J4.pin1, TMC2130_RA.VMOT, TMC2130_DEC.VMOT, J5.pin1, TMC2130_FOC.VMOT, C_150uf_LOWESR.+, C_150uf_LOWESR_2.+, C_150uf_LOWESR_3.+
  N45: Fuse1.Connector1, Switch.pin2
  N46: X1.1, J2.pin3, TMC2130_RA.2B, EN_EA_EB_X_A1_A2_B1_B2.pin1
  N47: X1.2, J2.pin4, TMC2130_RA.2A, EN_EA_EB_X_A1_A2_B1_B2.pin2
  N48: X1.4, J2.pin5, TMC2130_RA.1A, EN_EA_EB_X_A1_A2_B1_B2.pin3
  N49: X1.5, J2.pin6, TMC2130_RA.1B, EN_EA_EB_X_A1_A2_B1_B2.pin4
  N50: X2.1, J4.pin3, TMC2130_DEC.2B, EN_EA_EB_X_A1_A2_B1_B2_2.pin1
  N51: X2.2, J4.pin4, TMC2130_DEC.2A, EN_EA_EB_X_A1_A2_B1_B2_2.pin2
  N52: X2.4, J4.pin5, TMC2130_DEC.1A, EN_EA_EB_X_A1_A2_B1_B2_2.pin3
  N53: X2.5, J4.pin6, TMC2130_DEC.1B, EN_EA_EB_X_A1_A2_B1_B2_2.pin4
  N54: X3.1, J5.pin3, TMC2130_FOC.2B, EN_EA_EB_X_A1_A2_B1_B2_3.pin1
  N55: X3.2, J5.pin4, TMC2130_FOC.2A, EN_EA_EB_X_A1_A2_B1_B2_3.pin2
  N56: X3.4, J5.pin5, TMC2130_FOC.1A, EN_EA_EB_X_A1_A2_B1_B2_3.pin3
  N57: X3.5, J5.pin6, TMC2130_FOC.1B, EN_EA_EB_X_A1_A2_B1_B2_3.pin4
  N58: J1.pin7, J1.pin8
  N59: J2.pin9, EN_EA_EB_X_A1_A2_B1_B2.pin6
  N60: J2.pin10, EN_EA_EB_X_A1_A2_B1_B2.pin7
  N61: J2.pin11, EN_EA_EB_X_A1_A2_B1_B2.pin8
  N62: J3.pin7, J3.pin8
  N63: J4.pin9, EN_EA_EB_X_A1_A2_B1_B2_2.pin6
  N64: J4.pin10, EN_EA_EB_X_A1_A2_B1_B2_2.pin7
  N65: J4.pin11, EN_EA_EB_X_A1_A2_B1_B2_2.pin8
  N66: J5.pin9, EN_EA_EB_X_A1_A2_B1_B2_3.pin6
  N67: J5.pin10, EN_EA_EB_X_A1_A2_B1_B2_3.pin7
  N68: J5.pin11, EN_EA_EB_X_A1_A2_B1_B2_3.pin8
  N69: J6.pin7, J6.pin8

notes:
  D+ D-
  REFR
  REFL
  DRV_EN
  CLK16
  GND
  SDO
  SDI
  SCK
  CSN
  VCC_IO
  GPS
  SHC
  PPS RX TX GND 5V

custom parts:
  SilentStepStick TMC2130: The TMC2130 provides an integrated motor driver solution for 3D-Printing, Cameras, Scanners and other automated equipment applications. The device has an integrated microstepping indexer, the sensorless stall detection technology StallGuard2™, the sensorless load dependent current control CoolStep™ and the completely noiseless current control mode StealthChop™ and is intended to drive a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
